# Fritzing sketch PC_Matrix16x32_MEga2560_Tetris (saved by Fritzing 0.9.3b)
circuit board: 14.169cm x 6.45966cm
breadboards: 1

parts:
  J10 = screw terminal, 2 pins
  Power_plug1 = Power plug
  ESP8266 = ESP8266 WiFi Module [part_number=ESP8266]
  S1 = Pushbutton [package="[THT]"]
  R1 = Resistor [tolerance=±5% resistance=10k package=THT]
  R6 = Resistor [tolerance=±5% resistance=220 package=THT]
  LED1 = LED - 3mm [color="Red (633nm)" package="3 mm [THT]"]
  LED2 = LED - 3mm [color="Red (633nm)" package="3 mm [THT]"]
  R7 = Resistor [tolerance=±5% resistance=220 package=THT]
  DS2 = Schottky Diode [part_number=BAT85 package="300 mil [THT]"]
  R9 = Resistor [tolerance=±5% resistance=10k package=THT]
  R8 = Resistor [tolerance=±5% resistance=220 package=THT]
  DZ2 = Zener Diode [part_number=1N5226B breakdown_voltage=3.3V package="300 mil [THT]"]
  C3 = Ceramic Capacitor [capacitance=100nF package="200 mil [THT, multilayer]"]
  C2 = Electrolytic Capacitor [capacitance=10µF package="100 mil [THT, electrolytic]"]
  C1 = Electrolytic Capacitor [capacitance=10µF package="100 mil [THT, electrolytic]"]
  Pad1 = Pad [width=17.5298219766629 height=13.4636999996508 connect=center]
  R10 = Resistor [tolerance=±5% resistance=4.7k package=THT]
  R11 = Resistor [tolerance=±5% resistance=10k package=THT]
  R3 = Resistor [tolerance=±5% resistance=1k package=THT]
  R2 = Resistor [tolerance=±5% resistance=10k package=THT]
  DZ1 = Zener Diode [part_number=1N5226B breakdown_voltage=3.3V package="300 mil [THT]"]
  R5 = Resistor [tolerance=±5% resistance=220 package=THT]
  DS1 = Schottky Diode [part_number=BAT85 package="300 mil [THT]"]
  R4 = Resistor [tolerance=±5% resistance=10k package=THT]
  LM1117-3V3 = V_REG_LD1117VXX [package=78xxl]
  BlueTooth_module = JY-MCU
  J6 = female pin header, 10 pins [form="♀ (female)"]
  J5 = female pin header, 8 pins [form="♀ (female)"]
  J4 = female pin header, 8 pins [form="♀ (female)"]
  J7 = female pin header, 8 pins [form="♀ (female)"]
  J8 = female pin header, 8 pins [form="♀ (female)"]
  J9 = female pin header, 8 pins [form="♀ (female)"]
  J2 = double row female pin header, 36 pins [form="♀ (female)"]
  J1 = double row male pin header, 16 pins [form="♂ (male)"]
  J12 = male pin header, 8 pins [form="♂ (male)"]
  J11 = male pin header, 8 pins [form="♂ (male)"]
  J13 = male pin header, 10 pins [form="♂ (male)"]
  J14 = female pin header, 8 pins [form="♀ (female)"]
  J15 = female pin header, 8 pins [form="♀ (female)"]
  J16 = female pin header, 8 pins [form="♀ (female)"]
  J17 = double row male pin header, 36 pins [form="♂ (male)"]
  J3 = double row male pin header, 16 pins [form="♂ (male)"]  # not connected

nets:
  GND: J10.pin1, Power_plug1.GND, ESP8266.GND, S1.Pin_1, S1.Pin_2, R6.Pin_0, R7.Pin_0, DZ2.anode, C3.1, C2.-, C1.-, R11.Pin_1, DZ1.anode, LM1117-3V3.GND, BlueTooth_module.GND, J6.pin7, J9.pin2, J9.pin3, J1.pin2, J1.pin4, J1.pin6, J1.pin8, J13.pin7, J14.pin2, J14.pin3
  VCC: J10.pin2, Power_plug1.VCC, R1.Pin_1, LED2.anode, R9.Pin_1, C1.+, LM1117-3V3.IN, BlueTooth_module.VCC, J9.pin4, J14.pin4
  N1: ESP8266.RXD, DS1.anode, R4.Pin_0
  N2: ESP8266.VCC, C3.0, C2.+, Pad1.pad, R2.Pin_1, R4.Pin_1, LM1117-3V3.OUT
  N3: ESP8266.RST, R2.Pin_0
  N4: ESP8266.CH_PD, R3.Pin_0
  N5: ESP8266.TXD, DZ1.cathode, R5.Pin_0
  N6: S1.Pin_3, S1.Pin_4, R1.Pin_0, J9.pin6, J14.pin6
  N7: R6.Pin_1, LED1.cathode
  N8: LED1.anode, J6.pin6, J13.pin6
  N9: LED2.cathode, R7.Pin_1
  N10: DS2.cathode, J4.pin8, J11.pin8
  N11: DS2.anode, R9.Pin_0, BlueTooth_module.RX
  N12: R8.Pin_0, J4.pin7, J11.pin7
  N13: R8.Pin_1, DZ2.cathode, BlueTooth_module.TX
  N14: R10.Pin_0, J5.pin3, J12.pin3
  N15: R10.Pin_1, R11.Pin_0, BlueTooth_module.KEY
  N16: R3.Pin_1, J2.pin35, J17.pin35
  N17: R5.Pin_1, J4.pin5, J11.pin5
  N18: DS1.cathode, J4.pin6, J11.pin6
  N19: J6.pin1, J13.pin1
  N20: J6.pin2, J13.pin2
  N21: J6.pin3, J13.pin3
  N22: J6.pin4, J1.pin10, J13.pin4
  N23: J6.pin5, J13.pin5
  N24: J6.pin8, J13.pin8
  N25: J6.pin9, J13.pin9
  N26: J6.pin10, J13.pin10
  N27: J5.pin1, J12.pin1
  N28: J5.pin2, J12.pin2
  N29: J5.pin4, J12.pin4
  N30: J5.pin5, J12.pin5
  N31: J5.pin6, J12.pin6
  N32: J5.pin7, J12.pin7
  N33: J5.pin8, J12.pin8
  N34: J4.pin1, J11.pin1
  N35: J4.pin2, J11.pin2
  N36: J4.pin3, J11.pin3
  N37: J4.pin4, J11.pin4
  N38: J7.pin1, J16.pin1
  N39: J7.pin2, J16.pin2
  N40: J7.pin3, J16.pin3
  N41: J7.pin4, J16.pin4
  N42: J7.pin5, J16.pin5
  N43: J7.pin6, J16.pin6
  N44: J7.pin7, J16.pin7
  N45: J7.pin8, J16.pin8
  N46: J8.pin1, J15.pin1
  N47: J8.pin2, J15.pin2
  N48: J8.pin3, J15.pin3
  N49: J8.pin4, J15.pin4
  N50: J8.pin5, J15.pin5
  N51: J8.pin6, J15.pin6
  N52: J8.pin7, J15.pin7
  N53: J8.pin8, J15.pin8
  N54: J9.pin1, J14.pin1
  N55: J9.pin5, J14.pin5
  N56: J9.pin7, J14.pin7
  N57: J9.pin8, J14.pin8
  N58: J2.pin1, J2.pin36, J17.pin1, J17.pin36
  N59: J2.pin2, J17.pin2
  N60: J2.pin3, J1.pin3, J17.pin3
  N61: J2.pin4, J1.pin16, J17.pin4
  N62: J2.pin5, J1.pin15, J17.pin5
  N63: J2.pin6, J1.pin5, J17.pin6
  N64: J2.pin7, J1.pin7, J17.pin7
  N65: J2.pin8, J17.pin8
  N66: J2.pin9, J17.pin9
  N67: J2.pin10, J17.pin10
  N68: J2.pin11, J17.pin11
  N69: J2.pin12, J17.pin12
  N70: J2.pin13, J17.pin13
  N71: J2.pin14, J17.pin14
  N72: J2.pin15, J17.pin15
  N73: J2.pin16, J17.pin16
  N74: J2.pin17, J17.pin17
  N75: J2.pin18, J2.pin19, J17.pin18, J17.pin19
  N76: J2.pin20, J17.pin20
  N77: J2.pin21, J17.pin21
  N78: J2.pin22, J17.pin22
  N79: J2.pin23, J17.pin23
  N80: J2.pin24, J17.pin24
  N81: J2.pin25, J17.pin25
  N82: J2.pin26, J17.pin26
  N83: J2.pin27, J17.pin27
  N84: J2.pin28, J17.pin28
  N85: J2.pin29, J1.pin9, J17.pin29
  N86: J2.pin30, J1.pin11, J17.pin30
  N87: J2.pin31, J1.pin12, J17.pin31
  N88: J2.pin32, J1.pin1, J17.pin32
  N89: J2.pin33, J1.pin13, J17.pin33
  N90: J2.pin34, J1.pin14, J17.pin34

notes:
  R1
  G1
  B1
  GND
  R2
  G2
  B2
  A
  B
  C
  D
  CLK
  LAT
  OE

custom parts:
  ESP8266 WiFi Module: Generic WiFi Module based on the ESP8266 with onboard PCB antenna and UART communications
  V_REG_LD1117VXX: LD1117VXX voltage regulator. We carry the 3.3V version (COM-00526) in TO-220 package.
  JY-MCU: Description: The Bluetooth Mate is very similar to our BlueSMiRF modem, but it is designed specifically to be used with our Arduino Pros and LilyPad Arduinos. These modems work as a serial (RX/TX) pipe, and are a great wireless replacement for serial cables. Any serial stream from 9600 to 115200bps can be passed seamlessly from your computer to your target. Bluetooth Mate has the same pin out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
